# Fritzing sketch final (saved by Fritzing 0.9.3b)

parts:
  BeagleBone1 = BeagleBone Black
  Part1 = Soil Moisture Sensor
  Part2 = Lilypad Power Supply
  Part3 = Lilypad Power Supply
  M1 = DC Motor
  IC1 = L293D [package=THT]
  DHT1 = DHT22 Humidity and Temperature Sensor
  R1 = Photocell (LDR) [package=THT]
  R2 = Resistor [tolerance=±5% resistance=220 package="2010 [SMD]"]
  U1 = ESP8266 WiFi Module [part_number=ESP8266]

nets:
  N1: BeagleBone1.no_name_yet#1, DHT1.GND
  N2: BeagleBone1.no_name_yet#3, DHT1.VDD
  N3: BeagleBone1.no_name_yet#4, U1.VCC
  N4: BeagleBone1.no_name_yet#5, Part2.+
  N5: BeagleBone1.no_name_yet#6, U1.CH_PD
  N6: BeagleBone1.no_name_yet#10, U1.RST
  N7: BeagleBone1.no_name_yet#11, Part1.SIG
  N8: BeagleBone1.no_name_yet#12, R1.pin_0, R2.Pin_0
  N9: BeagleBone1.no_name_yet#22, IC1.Enable_2
  N10: BeagleBone1.no_name_yet#24, U1.GPIO_0
  N11: BeagleBone1.no_name_yet#26, U1.GPIO_2
  N12: BeagleBone1.no_name_yet#101, U1.GND
  N13: BeagleBone1.no_name_yet#102, Part2.GND, IC1.In_2
  N14: BeagleBone1.no_name_yet#112, DHT1.DATA
  N15: Part1.VCC, R1.pin_1
  N16: Part1.GND, R2.Pin_1
  N17: Part3.+, IC1.In_1
  N18: Part3.GND, IC1.0V
  N19: M1.pin_1, IC1.Out_4_(_Controlled_by_Enable_2_)
  N20: M1.pin_2, IC1.Out_3_(_Controlled_by_Enable_2_)

custom parts:
  BeagleBone Black: BeagleBone Black rev. A5B
  ESP8266 WiFi Module: Generic WiFi Module based on the ESP8266 with onboard PCB antenna and UART communications
